// Logisim project 4BitMIPS.circ as structural Verilog: 1 circuit, main circuit 4 Bit MIPS
module _4_Bit_MIPS (
  input  [7:0] in_1
);

  wire control_unit_1_alu_src, control_unit_1_memread, control_unit_1_memtoreg, control_unit_1_memwrite,
       control_unit_1_reg_dst, control_unit_1_regwrite;
  wire [2:0] control_unit_1_alu_op, instruction_memory_1_output_0;
  wire [3:0] data_memory_1_read_data, instruction_memory_1_output_1, instruction_memory_1_output_2,
       instruction_memory_1_output_3, n4bit_mux_1_y, n4bit_mux_2_y, n4bitalu_1_output, register_1_p4,
       register_1_p6, register_1_p7;
  wire [7:0] adder_1_out;
  wire [7:7] instruction_memory_1_output_0_2;

  Instruction_Memory instruction_memory_1 (
    .Input(in_1), .Output_0({instruction_memory_1_output_0_2[7], instruction_memory_1_output_0}),
    .Output_1(instruction_memory_1_output_1), .Output_2(instruction_memory_1_output_2),
    .Output_3(instruction_memory_1_output_3));
  Adder adder_1 (.a(in_1), .b(8'h1), .out(adder_1_out));  // open: cin, cout
  _4BIT_MUX u_4bit_mux_1 (
    .A(instruction_memory_1_output_1),
    .B({instruction_memory_1_output_0_2[7], instruction_memory_1_output_0}), .S(control_unit_1_reg_dst),
    .Y(n4bit_mux_1_y));
  Control_Unit control_unit_1 (
    .OPCode(instruction_memory_1_output_3), .RegWrite(control_unit_1_regwrite),
    .ALU_SRC(control_unit_1_alu_src), .ALU_OP(control_unit_1_alu_op), .MemToReg(control_unit_1_memtoreg),
    .MemWrite(control_unit_1_memwrite), .MemRead(control_unit_1_memread), .REG_DST(control_unit_1_reg_dst));  // open: out_2, JUMP, BNEQ, ALU0, ALU1, ALU2, BRANCH
  // Register register_1: pin names not known; wires that end beside it: instruction_memory_1_output_2, instruction_memory_1_output_1, n4bit_mux_1_y, register_1_p4, control_unit_1_regwrite, register_1_p6, register_1_p7
  _4BIT_MUX u_4bit_mux_2 (
    .A(register_1_p7), .B({instruction_memory_1_output_0_2[7], instruction_memory_1_output_0}),
    .S(control_unit_1_alu_src), .Y(n4bit_mux_2_y));
  _4BitALU u_4bitalu_1 (
    .A(register_1_p6), .B(n4bit_mux_2_y), .ALU_OpCode(control_unit_1_alu_op), .Output(n4bitalu_1_output));  // open: Overflow, Zero
  Adder adder_2 (
    .a(adder_1_out), .b({{5{instruction_memory_1_output_0_2[7]}}, instruction_memory_1_output_0}));  // open: out, cin, cout
  Data_Memory data_memory_1 (
    .Read_Data(data_memory_1_read_data), .Address(n4bitalu_1_output), .Write_Data(register_1_p7),
    .MemWrite(control_unit_1_memwrite), .MemRead(control_unit_1_memread));  // open: out_5, out_7, out_8, out_9, out_10, out_11, out_12, out_13, out_14, out_15, out_16, out_17, out_18
  _4BIT_MUX u_4bit_mux_3 (
    .A(n4bitalu_1_output), .B(data_memory_1_read_data), .S(control_unit_1_memtoreg), .Y(register_1_p4));
endmodule
