// Logisim project Data Memory.circ as structural Verilog: 1 circuit, main circuit main
module main (
  input  [3:0] in_1,
  output [11:0] out_2,
  output out_3,
  output out_4,
  output out_5,
  output out_6,
  output out_7,
  output out_8,
  output out_9,
  output out_10,
  output out_11,
  output out_12,
  output out_13,
  output out_14
);

  ROM #(.addrWidth(4), .dataWidth(12)) rom_1 (.addr(in_1), .data(out_2), .sel(1'b1));

  assign out_3 = out_2[0];
  assign out_4 = out_2[1];
  assign out_5 = out_2[2];
  assign out_6 = out_2[3];
  assign out_7 = out_2[4];
  assign out_8 = out_2[5];
  assign out_9 = out_2[6];
  assign out_10 = out_2[7];
  assign out_11 = out_2[8];
  assign out_12 = out_2[9];
  assign out_13 = out_2[10];
  assign out_14 = out_2[11];

  // Notes on the sheet:
  //   contents of rom_1 (hex, n*v repeats v):
  //   410 804 844 824 c 5c 108 814 1 834 6c 2c 412 1c 3c 28c
endmodule
