// Logisim project Instruction Memory.circ as structural Verilog: 1 circuit, main circuit Instruction Memory
module Instruction_Memory (
  input  [7:0] Input,
  output [3:0] Output_0,
  output [3:0] Output_1,
  output [3:0] Output_2,
  output [3:0] Output_3
);

  ROM #(.dataWidth(16)) rom_1 (.addr(Input), .data({Output_3, Output_2, Output_1, Output_0}), .sel(1'b1));

  // Notes on the sheet:
  //   contents of rom_1 (hex, n*v repeats v):
  //   410 2123 14*0 dfa1 7*0 ad
endmodule
