// Logisim project Register File.circ as structural Verilog: 1 circuit, main circuit Register
module Register (
  input  [3:0] Write_Data,
  input  [3:0] Write_Reg,
  input  Reg_Write,
  input  [3:0] Read_Reg_1,
  input  [3:0] Read_Reg_2,
  output [3:0] Read_Data_1,
  output [3:0] Read_Data_2
);

  wire clock_1_out, n7404_1_p2, n7404_1_p4, n7404_1_p6, n7404_1_p10, n7404_1_p12, n7404_1_p14, n74138_1_p9,
       n74138_1_p10, n74138_1_p11, n74138_1_p12, n74138_1_p13, n74138_1_p14;
  wire [3:0] sp_q, t0_q, t1_q, t2_q, t3_q, t4_q, Zero_q;

  Register_part #(.width(4)) Zero (.en(1'b0), .Q(Zero_q), .clk(clock_1_out), .clr(1'b1));  // open: D
  // _74138 74138_1: pin names not known; wires that end beside it: Write_Reg[0], Write_Reg[1], Write_Reg[2], Write_Reg[3], Reg_Write, 1'b1, 1'b0, 1'b1, n74138_1_p9, n74138_1_p10, n74138_1_p11, n74138_1_p12, n74138_1_p13, n74138_1_p14
  // _7404 7404_1: pin names not known; wires that end beside it: n74138_1_p12, n7404_1_p2, n74138_1_p13, n7404_1_p4, n74138_1_p14, n7404_1_p6, 1'b0, 1'b1, n74138_1_p9, n7404_1_p10, n74138_1_p10, n7404_1_p12, n74138_1_p11, n7404_1_p14
  Register_part #(.width(4)) t0 (.D(Write_Data), .en(n7404_1_p10), .Q(t0_q), .clk(clock_1_out), .clr(1'b0));
  Register_part #(.width(4)) t1 (.D(Write_Data), .en(n7404_1_p12), .Q(t1_q), .clk(clock_1_out), .clr(1'b0));
  Clock clock_1 (.out(clock_1_out));
  Register_part #(.width(4)) t2 (.D(Write_Data), .en(n7404_1_p14), .Q(t2_q), .clk(clock_1_out), .clr(1'b0));
  Register_part #(.width(4)) t3 (.D(Write_Data), .en(n7404_1_p2), .Q(t3_q), .clk(clock_1_out), .clr(1'b0));
  Register_part #(.width(4)) t4 (.D(Write_Data), .en(n7404_1_p4), .Q(t4_q), .clk(clock_1_out), .clr(1'b0));
  Register_part #(.width(4)) sp (.D(Write_Data), .en(n7404_1_p6), .Q(sp_q), .clk(clock_1_out), .clr(1'b0));
  _7_4__TO_1_4__MUX u_7_4_to_1_4_mux_1 (
    .in_1(Zero_q), .in_2(t0_q), .in_3(t1_q), .in_4(t2_q), .in_5(t3_q), .in_6(Read_Reg_1), .in_7(t4_q),
    .in_8(sp_q), .out_9(Read_Data_1));
  _7_4__TO_1_4__MUX u_7_4_to_1_4_mux_2 (
    .in_1(Zero_q), .in_2(t0_q), .in_3(t1_q), .in_4(t2_q), .in_5(t3_q), .in_6(Read_Reg_2), .in_7(t4_q),
    .in_8(sp_q), .out_9(Read_Data_2));
endmodule
