// Logisim project Sign Extender.circ as structural Verilog: 1 circuit, main circuit main
module main (
  input  [3:0] _4_Bit,
  output [7:0] _8_bit
);


  assign _8_bit = {{5{_4_Bit[3]}}, _4_Bit[2:0]};
endmodule
